# Fritzing sketch RPi_Airbox_Type1_DHT22_MQ2_SH1106 (saved by Fritzing 0.9.3b)
breadboards: 1

parts:
  Raspberry_Pi_1 = Raspberry Pi 3 [part_number=RPI-3-V1.2]
  Grove1 = Grove OLED 128x96
  RHT1 = Humidity and Temperature Sensor RHT03
  IC2 = MCP3008 8-channel 10-bit ADC [part_number=MCP3008]
  U1 = GAS_SENSOR [package=mq-3]
  R1 = Resistor [tolerance=±5% resistance=220 package="0603 [SMD]"]
  R2 = Resistor [tolerance=±5% resistance=220 package="2512 [SMD]"]
  R3 = Resistor [tolerance=±5% resistance=220 package="2010 [SMD]"]

nets:
  VCC: Raspberry_Pi_1.3v3, Raspberry_Pi_1.5V, Grove1.VCC, RHT1.Vcc, IC2.no_name_yet#15, IC2.no_name_yet#16, U1.B1, R3.Pin_1
  N1: Raspberry_Pi_1.GPIO2, Grove1.SDA
  GND: Raspberry_Pi_1.GPIO3, Raspberry_Pi_1.GIPO10, Raspberry_Pi_1.GND, Grove1.GND, Grove1.SCL, RHT1.GND_1, IC2.no_name_yet#9, IC2.no_name_yet#11, IC2.no_name_yet#14, U1.A1, R2.Pin_1
  N2: Raspberry_Pi_1.GIPO4, RHT1.Data-signal, R3.Pin_0
  N3: Raspberry_Pi_1.GIPO9, Raspberry_Pi_1.GIPO25, IC2.no_name_yet#12
  N4: Raspberry_Pi_1.GIPO11, Raspberry_Pi_1.GIPO7, IC2.no_name_yet#13
  N5: Raspberry_Pi_1.GIPO8, IC2.no_name_yet#10
  N6: IC2.no_name_yet#1, R1.Pin_1, R2.Pin_0
  N7: U1.H2, R1.Pin_0

notes:
  1KΩ
  2KΩ
  A0 Pin
  SH1106 OLED Screen
  DHT22
  MQ2
