# Fritzing sketch RPi_Airbox_Type2_DHT22_PMS3003_NEO6M (saved by Fritzing 0.9.3b)
breadboards: 1

parts:
  Raspberry_Pi_1 = Raspberry Pi 3 [part_number=RPI-3-V1.2]
  RHT1 = Humidity and Temperature Sensor RHT03
  R3 = Resistor [tolerance=±5% resistance=220 package="2010 [SMD]"]
  U1 = SUP500F [package=sup500f]
  USBTTL1 = USB TTL Serial Cable
  U3 = SUP500F [package=sup500f]
  元件1 = LCD1602-I2C

nets:
  3V3: Raspberry_Pi_1.3v3, Raspberry_Pi_1.3V3, RHT1.Vcc, R3.Pin_1, 元件1.VCC
  N1: Raspberry_Pi_1.GPIO2, 元件1.SDA
  N2: Raspberry_Pi_1.GPIO3, 元件1.SCL
  GND: Raspberry_Pi_1.GIPO4, Raspberry_Pi_1.GND, Raspberry_Pi_1.GIPO14, RHT1.Data-signal, RHT1.GND_1, RHT1.GND_2, R3.Pin_0, U3.GND, 元件1.GND
  N3: Raspberry_Pi_1.GIPO15, U3.TX-O
  5V: Raspberry_Pi_1.5V, U3.VCC
  N4: U1.RX-I, USBTTL1.TX
  N5: U1.TX-O, USBTTL1.RX
  GND_2: U1.GND, USBTTL1.GND
  VCC: U1.VCC, USBTTL1.5V

notes:
  DHT22
  uBlox Neo-6M
  GPS
  Plantower G3
  PMS3003
  Pin 5 Tx
  Pin 1
  Vcc

custom parts:
  LCD1602-I2C: A standard character display, usually with 2x16 characters. Comes in many colors with LCM1602 IIC attached.
